# Fritzing sketch adabox002-robot (saved by Fritzing 0.9.3b)
breadboards: 1

parts:
  Part1 = Adafruit DC+Stepper FeatherWing [part_number="Adafruit #2927"]
  J1 = Piezo Speaker
  LED1 = LED - 5mm [color="Green (555nm)" package="5 mm [THT]"]
  R1 = Resistor [tolerance=±5% resistance=560 package=THT]
  R2 = Resistor [tolerance=±5% resistance=560 package=THT]
  R3 = Resistor [tolerance=±5% resistance=560 package=THT]
  R4 = Resistor [tolerance=±5% resistance=560 package=THT]
  LED2 = LED - 5mm [color="Red (633nm)" package="5 mm [THT]"]
  LED3 = LED - 5mm [color="White (4500K)" package="5 mm [THT]"]
  LED4 = LED - 5mm [color="White (4500K)" package="5 mm [THT]"]

nets:
  N1: Part1.GND, J1.pin2, R1.Pin_0, R2.Pin_0, R3.Pin_0, R4.Pin_0
  N2: Part1.B, J1.pin1
  N3: Part1.J, LED3.anode
  N4: Part1.K, LED4.anode
  N5: Part1.L, LED1.anode
  N6: Part1.M, LED2.anode
  N7: LED1.cathode, R1.Pin_1
  N8: R2.Pin_1, LED3.cathode
  N9: R3.Pin_1, LED4.cathode
  N10: R4.Pin_1, LED2.cathode

custom parts:
  Adafruit DC+Stepper FeatherWing: This is the DC Motor + Stepper FeatherWing which will let you use 2 x bi-polar stepper motors or 4 x brushed DC motorx (or 1 stepper and 2 DC motors). Using our Feather Stacking Headers or Feather Female Headers you can connect a FeatherWing on top or bottom of your Feather board and let the board take flight! The original Adafruit Motorshield Kit is one of our most beloved kits, which is why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
